// Logisim project CircuitosArq-CC4.circ as structural Verilog: 6 circuits, main circuit main
module main (
  input  [1:0] xy,
  input  [3:0] B,
  input  [3:0] A
);
endmodule

module add_1 (
  input  a,
  input  b,
  input  c,
  output s,
  output c_2
);

  wire and_1_out, and_2_out, and_3_out, and_4_out, and_5_out, and_6_out, and_7_out, not_1_out, not_2_out,
       not_3_out, not_4_out, not_5_out, not_6_out;

  not not_1 (not_1_out, a);
  not not_2 (not_2_out, b);
  not not_3 (not_3_out, a);
  not not_4 (not_4_out, c);
  not not_5 (not_5_out, b);
  not not_6 (not_6_out, c);
  and and_1 (and_1_out, b, c);
  and and_2 (and_2_out, a, c);
  and and_3 (and_3_out, a, b);
  and and_4 (and_4_out, not_1_out, not_2_out, c);
  and and_5 (and_5_out, not_3_out, b, not_4_out);
  and and_6 (and_6_out, a, not_5_out, not_6_out);
  and and_7 (and_7_out, a, b, c);
  or or_1 (c_2, and_1_out, and_2_out, and_3_out);
  or or_2 (s, and_4_out, and_5_out, and_6_out, and_7_out);
endmodule

module add_4 (
  input  [3:0] B,
  input  [3:0] A,
  output Overflow,
  output [3:0] S
);

  wire add_1_2_c_2, add_1_3_c_2, add_1_4_c_2;

  add_1 add_1_1 (.a(A[3]), .b(B[3]), .c(add_1_2_c_2), .s(S[3]), .c_2(Overflow));
  add_1 add_1_2 (.a(A[2]), .b(B[2]), .c(add_1_3_c_2), .s(S[2]), .c_2(add_1_2_c_2));
  add_1 add_1_3 (.a(A[1]), .b(B[1]), .c(add_1_4_c_2), .s(S[1]), .c_2(add_1_3_c_2));
  add_1 add_1_4 (.a(A[0]), .b(B[0]), .c(1'b0), .s(S[0]), .c_2(add_1_4_c_2));
endmodule

module buffer (
  input  [3:0] E,
  input  Control,
  output [3:0] S
);

  assign S[1] = Control ? E[1] : 1'bz;  // Controlled_Buffer controlled_buffer_1
  assign S[2] = Control ? E[2] : 1'bz;  // Controlled_Buffer controlled_buffer_2
  assign S[3] = Control ? E[3] : 1'bz;  // Controlled_Buffer controlled_buffer_3
  assign S[0] = Control ? E[0] : 1'bz;  // Controlled_Buffer controlled_buffer_4
endmodule

module sub_1 (
  input  A,
  input  B,
  input  C,
  output S,
  output Vai_1
);

  wire and_1_out, and_2_out, or_1_out, xor_1_out;

  xor xor_1 (xor_1_out, C, B);
  or or_1 (or_1_out, C, B);
  xor xor_2 (S, xor_1_out, A);
  and and_1 (and_1_out, or_1_out, ~A);  // AND_Gate
  and and_2 (and_2_out, C, B);
  or or_2 (Vai_1, and_1_out, and_2_out);
endmodule

module sub_4 (
  input  [3:0] in_1,
  input  [3:0] in_2,
  output out_3,
  output [3:0] out_4
);

  wire sub_1_2_vai_1, sub_1_3_vai_1, sub_1_4_vai_1;

  sub_1 sub_1_1 (.S(out_4[3]), .Vai_1(out_3), .A(in_2[3]), .B(in_1[3]), .C(sub_1_2_vai_1));
  sub_1 sub_1_2 (.S(out_4[2]), .Vai_1(sub_1_2_vai_1), .A(in_2[2]), .B(in_1[2]), .C(sub_1_3_vai_1));
  sub_1 sub_1_3 (.S(out_4[1]), .Vai_1(sub_1_3_vai_1), .A(in_2[1]), .B(in_1[1]), .C(sub_1_4_vai_1));
  sub_1 sub_1_4 (.S(out_4[0]), .Vai_1(sub_1_4_vai_1), .A(in_2[0]), .B(in_1[0]), .C(1'b0));
endmodule
